# Fritzing sketch FIKIRA (saved by Fritzing 0.9.4)
circuit board: 8.46667cm x 5.64444cm
breadboards: 1

parts:
  A1 = u-blox NEO-6M GPS Breakout
  DHT1 = Humidity and Temperature Sensor DHT11
  WeMos_D1_Mini1 = WeMos D1 Mini
  S1 = Round Pushbutton
  J1 = Power Jack [package=power_jack_pth]
  IC1 = Voltage Regulator [package=78xxl]
  C3 = Electrolytic Capacitor [capacitance=0.22mF voltage=35V package="100 mil [THT, electrolytic]"]
  C4 = Electrolytic Capacitor [capacitance=1µF voltage=10V package="100 mil [THT, electrolytic]"]
  U1 = LIPO-2000mAh [package=lipo-2000]
  LED1 = LEDs [package=led10mm]
  LED2 = LEDs [package=led10mm]
  R1 = Resistor [tolerance=±5% resistance=220 package=THT]
  R2 = Resistor [tolerance=±5% resistance=220 package=THT]
  D3 = Diode [package=diode-1n4148]
  Part2 = Soil Moisture Sensor

nets (from the breadboard view):
  VCC: A1.Pin_1, DHT1.Vcc, S1.leg0, R2.Pin_0, Part2.VCC
  GND: A1.Pin_2, DHT1.GND_1, WeMos_D1_Mini1.G, J1.GND, J1.GNDBREAK, IC1.GND, C3.-, U1.-, LED1.C, Part2.GND
  N1: A1.Pin_3, WeMos_D1_Mini1.D5
  N2: A1.Pin_4, WeMos_D1_Mini1.D6
  N3: DHT1.Data-signal, WeMos_D1_Mini1.D4
  N4: WeMos_D1_Mini1.A0, Part2.SIG
  N5: S1.leg1, U1.+, D3.C
  N6: J1.PWR, IC1.IN, C3.+
  N7: IC1.OUT, C4.+, R1.Pin_0, D3.A
  N8: C4.-, LED2.C
  N9: LED1.A, R2.Pin_1
  N10: LED2.A, R1.Pin_1

custom parts:
  Humidity and Temperature Sensor DHT11: Digital relative humidity & temperature sensor DHT11
  Voltage Regulator: Voltage Regulator Standard 7805 5V regulator. IGO (Input Ground Output). Spark Fun Electronics SKU : COM-00107
